# Fritzing sketch logger_v3 (saved by Fritzing 0.9.3b)

parts:
  OLED1 = SSD1306 0.96in 128x64 I2C Monochrome OLED Display
  Mod1 = Full Size SD Card Module
  Part1 = ADS1115
  U1 = LuaNode32 / ESP32 [part_number=ESP32S-PIN30]
  ZS-042_RTC1 = ZS-042 RTC Module

nets:
  N1: OLED1.SCL, U1.D22
  N2: OLED1.SDA, U1.D21
  N3: Mod1.pin_1, U1.GND
  N4: Mod1.pin_3, Mod1.pin_4, U1.3V3
  N5: Mod1.pin_7, U1.D5
  N6: Mod1.pin_9, U1.D23
  N7: Mod1.pin_11, U1.D18
  N8: Mod1.pin_13, U1.D19
  N9: Part1.SCL, U1.D32
  N10: Part1.SDA, U1.D33
  N11: Part1.ALRT, U1.D4
  N12: U1.D25, ZS-042_RTC1.SCL
  N13: U1.D26, ZS-042_RTC1.SDA

custom parts:
  Full Size SD Card Module: SD Card Module Slot Socket Reader For Arduino ARM MCU
  ADS1115: ADC ADS1115
  LuaNode32 / ESP32: New Image for LuaNode32 DOIT ESP32 DEVKIT V1. Base parts from LuaNode32 / ESP32 ESP32 based LuaNode32 by G.Noorlander DOIT Esp32 DevKit v1 (30 pins long, 11 pins width) by Werner Rothschopf (modified by vanepp Dec 2018)
